# Fritzing sketch PTC2(7segment) (saved by Fritzing 0.9.4)

parts:
  U1 = ESP32-38PinWide [part_number=ESP32-38PinWide]
  S1 = Pushbutton [package="[THT]"]
  LED1 = smd LED [color="Green (560nm)" package="0805 [SMD]"]
  Part1 = TM1637

nets:
  N1: U1.GPIO13, LED1.anode
  N2: U1.GPIO9, S1.Pin_1, S1.Pin_2
  N3: U1.GPIO11, Part1.VCC
  VIN: U1.VIN, Part1.GND
  N4: U1.GPIO15, Part1.CLK
  N5: U1.GPIO2, Part1.DIO
  N6: U1.GND, S1.Pin_3, LED1.cathode

notes:
  4-segment TM1637 - RM4.90
  ESP32 - RM27.26
  PB - RM0.40
  LED - RM0.10

custom parts:
  ESP32-38PinWide: Generic 38-Pin ESP32 with wide format (only access to one side of pins on a breadboard) based on Stephen Lilley's HiLetgo ESP-WROOM-32 ESP32 ESP-32S Development Board.
  TM1637: A 4 7-seg display
